// Logisim project counter-stop.circ as structural Verilog: 1 circuit, main circuit main
module main (
  output [1:0] count,
  output halt
);

  wire _mcp_a7eed291cff4_0;

  Clock #(.highDuration(1), .lowDuration(1)) clock_1 (.out(_mcp_a7eed291cff4_0));
  Counter #(.width(2), .max('h3), .ongoal("wrap"), .trigger("rising"), .behavior("new")) counter_1 (
    .load(1'b0), .D(2'b00), .count(1'b0), .Q(count), .carry(halt), .up(1'b1), .clk(_mcp_a7eed291cff4_0),
    .clr(1'b0));

  // Other names for the same wires on the sheet: _mcp_a7eed291cff4_4[1:0] = count; _mcp_a7eed291cff4_5 = halt
endmodule
