// Logisim project full-adder.circ as structural Verilog: 2 circuits, main circuit main
module main (
  input  A,
  input  B,
  input  Cin,
  output S,
  output C,
  output halt
);

  FA fa_1 (.A(A), .B(B), .Cin(Cin), .S(S), .C(C));

  assign halt = 1'b1;

  // Other names for the same wires on the sheet: _mcp_d94d85213d3f_0 = A; _mcp_d94d85213d3f_1 = B;
  //   _mcp_d94d85213d3f_2 = Cin; _mcp_d94d85213d3f_3 = S; _mcp_d94d85213d3f_4 = C
endmodule

module FA (
  input  A,
  input  B,
  input  Cin,
  output S,
  output C
);

  wire _mcp_4a7d5c9d54ad_3, _mcp_4a7d5c9d54ad_4, _mcp_4a7d5c9d54ad_5;

  xor xor_1 (_mcp_4a7d5c9d54ad_3, A, B);
  and and_1 (_mcp_4a7d5c9d54ad_4, A, B);
  xor xor_2 (S, _mcp_4a7d5c9d54ad_3, Cin);
  and and_2 (_mcp_4a7d5c9d54ad_5, _mcp_4a7d5c9d54ad_3, Cin);
  or or_1 (C, _mcp_4a7d5c9d54ad_4, _mcp_4a7d5c9d54ad_5);

  // Other names for the same wires on the sheet: _mcp_4a7d5c9d54ad_0 = A; _mcp_4a7d5c9d54ad_1 = B;
  //   _mcp_4a7d5c9d54ad_2 = Cin; _mcp_4a7d5c9d54ad_6 = S; _mcp_4a7d5c9d54ad_7 = C
endmodule
